// Logisim project 03_1.circ as structural Verilog: 1 circuit, main circuit main
module main (
  input  S_1,
  input  S_0,
  input  D
);

  wire and_1_out, and_2_out, and_3_out, and_4_out, not_1_out, not_2_out;

  not not_1 (not_1_out, S_1);
  not not_2 (not_2_out, S_0);
  and and_1 (and_1_out, S_1, S_0, D);
  and and_2 (and_2_out, not_1_out, S_0, D);
  and and_3 (and_3_out, S_1, not_2_out, D);
  // Probe on and_4_out
  and and_4 (and_4_out, not_1_out, not_2_out, D);
  // Probe on and_2_out
  // Probe on and_3_out
  // Probe on and_1_out
  // AND_Gate and_5 is placed but not wired

  // Notes on the sheet:
  //   S_1
  //   S_0
  //   D
endmodule
