// Logisim project 03_4.circ as structural Verilog: 1 circuit, main circuit main
module main (
  input  in_1,
  input  in_2,
  input  in_3,
  input  a,
  input  b,
  input  c,
  input  d,
  input  S_1,
  input  S_0
);

  wire multiplexer_1_out, multiplexer_2_out, multiplexer_3_out, multiplexer_4_out;

  Multiplexer multiplexer_1 (.in0(in_1), .in1(in_2), .out(multiplexer_1_out), .sel(in_3));
  Multiplexer multiplexer_2 (.in0(a), .in1(b), .out(multiplexer_2_out), .sel(S_0));
  Multiplexer multiplexer_3 (.in0(c), .in1(d), .out(multiplexer_3_out), .sel(S_0));
  // Probe on multiplexer_1_out
  // Probe on multiplexer_4_out
  Multiplexer multiplexer_4 (.in0(multiplexer_2_out), .in1(multiplexer_3_out), .out(multiplexer_4_out), .sel(S_1));
endmodule
